# Fritzing sketch temp-humidity-module (saved by Fritzing 0.9.2b)
breadboards: 1

parts:
  Raspberry_Pi1 = Raspberry Pi 2
  T1 = LM35 Temperature Sensor [package="TO92 [THT]"]

nets:
  N1: Raspberry_Pi1.3v3, T1.Vout
  N2: Raspberry_Pi1.GPIO14, T1.GND
  N3: Raspberry_Pi1.GND, T1.+Vs
