# Fritzing sketch rgb-led-modul (saved by Fritzing 0.9.2b)
breadboards: 1

parts:
  Raspberry_Pi_B_rev1 = Raspberry Pi B rev1
  U1 = QRD1114 [package=qrd1114]

nets:
  N1: Raspberry_Pi_B_rev1.GND, U1.A
  N2: Raspberry_Pi_B_rev1.GPIO_14, U1.K
  N3: Raspberry_Pi_B_rev1.GPIO_15, U1.E
  N4: Raspberry_Pi_B_rev1.GPIO_18, U1.C
